// Logisim project ALU-Input.circ as structural Verilog: 2 circuits, main circuit ALU-Input
module ALU_Input (
  input  [31:0] Rt,
  input  Type_I,
  input  [15:0] Const,
  input  Const_Extender_Selector,
  output [31:0] B
);

  wire [31:0] Const_t;

  Const_Extender const_extender_1 (.in_1(Const_Extender_Selector), .in_2(Const), .out_3(Const_t));
  Multiplexer #(.width(32), .enable("false")) multiplexer_1 (.in0(Rt), .in1(Const_t), .out(B), .sel(Type_I));

  // Notes on the sheet:
  //   ALU-Input
endmodule

module Const_Extender (
  input  in_1,
  input  [15:0] in_2,
  output [31:0] out_3
);

  wire and_1_out;

  and and_1 (and_1_out, ~in_1, in_2[15]);  // AND_Gate
  assign out_3 = {{16{and_1_out}}, in_2};  // Bit_Extender bit_extender_1

  // Other names for the same wires on the sheet: const[15:0] = in_2; I15 = in_2[15]; Output[31:0] = out_3;
  //   Selector = in_1
endmodule
