// Logisim project ALU-Selector.circ as structural Verilog: 2 circuits, main circuit ALU-Operation-Selector
module ALU_Operation_Selector (
  input  add,
  input  sub,
  input  slt,
  input  sltu,
  input  \and ,
  input  \or ,
  input  \nor ,
  input  \xor ,
  input  mult,
  input  mulu,
  input  div,
  input  divu,
  output [3:0] ALU_Op_Selector
);

  wire priority_encoder_1_gs;
  wire [3:0] priority_encoder_1_out;

  Priority_Encoder #(.select(4), .disabled(0)) priority_encoder_1 (
    .in0(add), .in1(sub), .in2(slt), .in3(sltu), .in4(\and ), .in5(\or ), .in6(\nor ), .in7(\xor ),
    .in8(mult), .in9(mulu), .in10(div), .in11(divu), .out(priority_encoder_1_out),
    .gs(priority_encoder_1_gs), .en_in(1'b1));  // open: in12, in13, in14, in15, en_out
  Multiplexer #(.width(4), .enable("false")) multiplexer_1 (
    .in0(4'b0000), .in1(priority_encoder_1_out), .out(ALU_Op_Selector), .sel(priority_encoder_1_gs));

  // Notes on the sheet:
  //   ALU Operations
endmodule

module Const_Extender_Selector (
  input  andi,
  input  ori,
  input  xori,
  output Selector
);

  or or_1 (Selector, andi, ori, xori);
endmodule
