// Logisim project ALU.circ as structural Verilog: 6 circuits, main circuit Multiplication
module ALU (
  input  [31:0] Data_A,
  input  [31:0] Data_B,
  input  [3:0] Selector,
  output [31:0] ALU_Output,
  output [31:0] High,
  output Zero_Flag,
  output Negative_Flag
);

  wire slt_bit, sltu_bit;
  wire [1:0] MultDivSelector;
  wire [31:0] Add, And, DivHigh, DivLow, DivuHigh, DivuLow, Low, MultHigh, MultLow, MuluHigh, MuluLow, Nor,
       Operations, Or, slt, sltu, Sub, Xor;

  Adder #(.width(32)) adder_1 (.a(Data_A), .b(Data_B), .out(Add));  // open: cin, cout
  Multiplier #(.width(32)) multiplier_1 (.a(Data_A), .b(Data_B), .out(MuluLow), .cout(MuluHigh));  // open: cin
  Multiplication multiplication_1 (.A(Data_A), .B(Data_B), .Low(MultLow), .High(MultHigh));
  Comparator #(.width(32)) comparator_1 (.a(Data_A), .b(Data_B), .lt(slt_bit));  // open: gt, eq
  assign slt = {{31{1'b0}}, slt_bit};  // Bit_Extender bit_extender_1
  Multiplexer #(.select(2), .width(32), .enable("false")) multiplexer_1 (
    .in0(MultHigh), .in1(DivHigh), .in2(MuluHigh), .in3(DivuHigh), .out(High), .sel(MultDivSelector));
  or or_1 (MultDivSelector[0], Selector[1], Selector[2]);
  or or_2 (MultDivSelector[1], Selector[0], Selector[2]);
  Subtractor #(.width(32)) subtractor_1 (.a(Data_A), .b(Data_B), .out(Sub));  // open: bin, bout
  Divider #(.width(32)) divider_1 (.a(Data_A), .b(Data_B), .out(DivuLow), .rem(DivuHigh));  // open: upper
  Division division_1 (.A(Data_A), .B(Data_B), .Low(DivLow), .High(DivHigh));
  Comparator #(.width(32), .mode("unsigned")) comparator_2 (.a(Data_A), .b(Data_B), .lt(sltu_bit));  // open: gt, eq
  assign sltu = {{31{1'b0}}, sltu_bit};  // Bit_Extender bit_extender_2
  Multiplexer #(.select(2), .width(32), .enable("false")) multiplexer_2 (
    .in0(MultLow), .in1(DivLow), .in2(MuluLow), .in3(DivuLow), .out(Low), .sel(MultDivSelector));
  Multiplexer #(.select(3), .width(32), .enable("false")) multiplexer_3 (
    .in0(Add), .in1(Sub), .in2(slt), .in3(sltu), .in4(And), .in5(Or), .in6(Nor), .in7(Xor), .out(Operations),
    .sel(Selector[2:0]));
  assign And = Data_A & Data_B;  // AND_Gate and_1, 32 bits wide
  assign Or = Data_A | Data_B;  // OR_Gate or_3, 32 bits wide
  Multiplexer #(.width(32), .enable("false")) multiplexer_4 (
    .in0(Operations), .in1(Low), .out(ALU_Output), .sel(Selector[3]));
  assign Nor = ~(Data_A | Data_B);  // NOR_Gate nor_1, 32 bits wide
  assign Xor = Data_A ^ Data_B;  // XOR_Gate xor_1, 32 bits wide
  Comparator #(.width(32)) comparator_3 (
    .a(ALU_Output), .b({32{1'b0}}), .eq(Zero_Flag), .lt(Negative_Flag));  // open: gt

  // Other names for the same wires on the sheet: A[31:0] = Data_A; B[31:0] = Data_B; Output[31:0] = ALU_Output;
  //   Selector_t[2:0] = Selector[2:0]; IsMultDiv = Selector[3]

  // Notes on the sheet:
  //   INPUTS
  //   ARITHMETIC
  //   LOGIC
  //   OUTPUTS
endmodule

module Multiplication (
  input  [31:0] A,
  input  [31:0] B,
  output [31:0] Low,
  output [31:0] High
);

  wire carry_low, NegOut, selectorA, selectorB;
  wire [31:0] adder_1_out, adder_2_out, multiplexer_1_out, multiplexer_2_out, multiplier_1_cout,
       multiplier_1_out, not_1_out, not_2_out, not_3_out, not_4_out;

  // Probe on A
  // Probe on B
  Comparator #(.width(1), .mode("unsigned")) comparator_1 (.a(1'b1), .b(A[31]), .eq(selectorA));  // open: gt, lt
  assign not_1_out = ~A;  // NOT_Gate not_1, 32 bits wide
  assign not_2_out = ~B;  // NOT_Gate not_2, 32 bits wide
  Comparator #(.width(1)) comparator_2 (.a(B[31]), .b(1'b1), .eq(selectorB));  // open: gt, lt
  Multiplexer #(.width(32), .enable("false")) multiplexer_1 (
    .in0(A), .in1(not_1_out), .out(multiplexer_1_out), .sel(selectorA));
  Multiplexer #(.width(32), .enable("false")) multiplexer_2 (
    .in0(B), .in1(not_2_out), .out(multiplexer_2_out), .sel(selectorB));
  Multiplier #(.width(32)) multiplier_1 (
    .a(multiplexer_1_out), .b(multiplexer_2_out), .out(multiplier_1_out), .cout(multiplier_1_cout));  // open: cin
  xor xor_1 (NegOut, selectorA, selectorB);
  assign not_3_out = ~multiplier_1_out;  // NOT_Gate not_3, 32 bits wide
  assign not_4_out = ~multiplier_1_cout;  // NOT_Gate not_4, 32 bits wide
  Adder #(.width(32)) adder_1 (.a(not_3_out), .b(32'h1), .out(adder_1_out), .cout(carry_low));  // open: cin
  Adder #(.width(32)) adder_2 (.a(not_4_out), .b({32{1'b0}}), .out(adder_2_out), .cin(carry_low));  // open: cout
  // Probe on Low
  Multiplexer #(.width(32), .enable("false")) multiplexer_3 (
    .in0(multiplier_1_out), .in1(adder_1_out), .out(Low), .sel(NegOut));
  Multiplexer #(.width(32), .enable("false")) multiplexer_4 (
    .in0(multiplier_1_cout), .in1(adder_2_out), .out(High), .sel(NegOut));
  // Probe on High
endmodule

module Division (
  input  [31:0] A,
  input  [31:0] B,
  output [31:0] Low,
  output [31:0] High
);

  wire is_zero;
  wire [1:0] selector;
  wire [31:0] cte, minus_neg_division, minus_positive_division, multiplexer_1_out, multiplexer_2_out,
       multiplication_1_low, neg_division, not_3_out, not_4_out, positive_division, rest;

  // Probe on A
  // Probe on B
  assign minus_positive_division = ~positive_division;  // NOT_Gate not_1, 32 bits wide
  Adder #(.width(32)) adder_1 (.a(positive_division), .b(cte), .out(neg_division));  // open: cin, cout
  assign minus_neg_division = ~neg_division;  // NOT_Gate not_2, 32 bits wide
  Comparator #(.width(1), .mode("unsigned")) comparator_1 (.a(1'b1), .b(A[31]), .eq(selector[1]));  // open: gt, lt
  assign not_3_out = ~A;  // NOT_Gate not_3, 32 bits wide
  assign not_4_out = ~B;  // NOT_Gate not_4, 32 bits wide
  Comparator #(.width(1)) comparator_2 (.a(B[31]), .b(1'b1), .eq(selector[0]));  // open: gt, lt
  Comparator #(.width(32)) comparator_3 (.a(rest), .b({32{1'b0}}), .eq(is_zero));  // open: gt, lt
  Multiplexer #(.width(32), .enable("false")) multiplexer_1 (
    .in0(A), .in1(not_3_out), .out(multiplexer_1_out), .sel(selector[1]));
  Multiplexer #(.width(32), .enable("false")) multiplexer_2 (
    .in0(B), .in1(not_4_out), .out(multiplexer_2_out), .sel(selector[0]));
  Divider #(.width(32)) divider_1 (
    .a(multiplexer_1_out), .b(multiplexer_2_out), .out(positive_division), .rem(rest));  // open: upper
  Multiplexer #(.width(32), .enable("false")) multiplexer_3 (.in0(32'h1), .in1({32{1'b0}}), .out(cte), .sel(is_zero));
  Multiplication multiplication_1 (.A(B), .B(Low), .Low(multiplication_1_low));  // open: High
  Multiplexer #(.select(2), .width(32), .enable("false")) multiplexer_4 (
    .in0(positive_division), .in1(minus_positive_division), .in2(minus_neg_division), .in3(neg_division),
    .out(Low), .sel(selector));
  Subtractor #(.width(32)) subtractor_1 (.a(A), .b(multiplication_1_low), .out(High));  // open: bin, bout
  // Probe on High
  // Probe on Low

  // Other names for the same wires on the sheet: result[31:0] = Low; selectorB = selector[0]; selectorA = selector[1]
endmodule

module ConstExtender (
  input  [15:0] in_1,
  input  in_2,
  input  in_3,
  input  in_4,
  output [31:0] out_5
);

  wire and_1_out, Selector;

  or or_1 (Selector, in_2, in_3, in_4);
  and and_1 (and_1_out, ~Selector, in_1[15]);  // AND_Gate
  assign out_5 = {{16{and_1_out}}, in_1};  // Bit_Extender bit_extender_1

  // Other names for the same wires on the sheet: andi = in_2; const[15:0] = in_1; I15 = in_1[15]; ori = in_3;
  //   Output[31:0] = out_5; xori = in_4
endmodule

module ALU_Encoder (
  input  add,
  input  \and ,
  input  addi,
  input  andi,
  input  mult,
  input  sub,
  input  \or ,
  input  mulu,
  input  ori,
  input  slt,
  input  slti,
  input  div,
  input  \nor ,
  input  sltu,
  input  \xor ,
  input  divu,
  input  sltui,
  input  xori,
  output [3:0] ALU_Selector
);

  wire add_t, and_t, or_t, slt_t, sltu_t, xor_t;

  or or_1 (add_t, add, addi);
  or or_2 (slt_t, slt, slti);
  or or_3 (sltu_t, sltu, sltui);
  or or_4 (ALU_Selector[0], sub, sltu_t, xor_t, or_t, mulu);
  or or_5 (and_t, \and , andi);
  or or_6 (or_t, \or , ori);
  or or_7 (xor_t, \xor , xori);
  or or_8 (ALU_Selector[1], slt_t, sltu_t, \nor , xor_t, div);
  or or_9 (ALU_Selector[2], and_t, or_t, \nor , xor_t, divu);
  or or_10 (ALU_Selector[3], mult, mulu, div, divu);

  // Other names for the same wires on the sheet: _0 = ALU_Selector[0]; _1 = ALU_Selector[1]; _2 = ALU_Selector[2];
  //   _3 = ALU_Selector[3]; sltiu = sltui

  // Notes on the sheet:
  //   ALU Operations
  //   Encoding
  //   Crafting Selector
endmodule

module Negative_To_Positive (
  input  [31:0] A,
  output [31:0] Output,
  output Negative
);

  wire [31:0] adder_1_out, not_1_out;

  // Probe on A
  assign not_1_out = ~A;  // NOT_Gate not_1, 32 bits wide
  Adder #(.width(32)) adder_1 (.a(not_1_out), .b(32'h1), .out(adder_1_out));  // open: cin, cout
  Multiplexer #(.width(32), .enable("false")) multiplexer_1 (.in0(A), .in1(adder_1_out), .out(Output), .sel(A[31]));
  // Probe on Output

  assign Negative = A[31];
endmodule
