// Logisim project Branch-Control-Selector.circ as structural Verilog: 1 circuit, main circuit Branch-Control-Selector
module Branch_Control_Selector (
  input  beq,
  input  bne,
  input  blez,
  input  bgtz,
  input  bltz,
  input  jr,
  input  j,
  output [2:0] Flag_Condition,
  output [1:0] BC_Selector
);

  wire IsBranch;
  wire [2:0] priority_encoder_1_out;

  or or_1 (BC_Selector[0], IsBranch, jr);
  or or_2 (BC_Selector[1], jr, j);
  Priority_Encoder priority_encoder_1 (
    .in0(beq), .in1(bne), .in2(bgtz), .in3(blez), .in4(bltz), .out(priority_encoder_1_out), .en_in(1'b1),
    .gs(IsBranch));  // open: in5, in6, in7, en_out
  Multiplexer #(.width(3), .enable("false")) multiplexer_1 (
    .in0(3'b000), .in1(priority_encoder_1_out), .out(Flag_Condition), .sel(IsBranch));

  // Notes on the sheet:
  //   Branch-Control-Selector
endmodule
