// Logisim project Control Unit.circ as structural Verilog: 1 circuit, main circuit main
module main (
  input  clock,
  input  reset,
  input  is_kbd,
  input  is_tty,
  input  is_RF,
  input  is_jump,
  input  is_read,
  input  is_write,
  input  use_HI_LO,
  input  ready_read,
  input  ready_write,
  input  halt,
  output get_data,
  output write_data,
  output PC_enable,
  output RF_enable,
  output Inst__Memory_enable,
  output tty_enable,
  output kbd_enable,
  output \end ,
  output HI_LO_en,
  output is_inst
);

  wire demultiplexer_2_out0, demultiplexer_2_out1, demultiplexer_3_out0, demultiplexer_3_out1,
       demultiplexer_5_out0, demultiplexer_6_out3, END_q, end_read, end_write, Fetch_instruction_q,
       get_data1, get_data_2, Idle_q, is_PC, MEM, mem_t, multiplexer_1_out, not_1_out, or_2_out, or_3_out,
       PC, RF, Save_inst_q, Save_q, wait_for_RAM_q;
  wire [1:0] exe_select;

  or or_1 (MEM, is_write, is_read);
  or or_2 (or_2_out, demultiplexer_2_out0, reset);
  or or_3 (or_3_out, demultiplexer_3_out0, mem_t);
  Demultiplexer #(.enable("false")) demultiplexer_1 (.out0(get_data_2), .out1(write_data), .in(mem_t), .sel(is_write));
  nor nor_1 (is_PC, MEM, is_RF);
  Demultiplexer #(.enable("false")) demultiplexer_2 (
    .out0(demultiplexer_2_out0), .out1(demultiplexer_2_out1), .in(Idle_q), .sel(not_1_out));
  D_Flip_Flop Idle (.clk(clock), .D(or_2_out), .Q(Idle_q));  // open: Qn, preset, en, reset
  or or_4 (get_data, get_data1, get_data_2);
  and and_1 (kbd_enable, PC_enable, is_kbd);
  not not_1 (not_1_out, reset);
  D_Flip_Flop wait_for_RAM (.clk(clock), .D(or_3_out), .Q(wait_for_RAM_q), .reset(reset));  // open: Qn, preset, en
  or or_5 (get_data1, PC_enable, demultiplexer_2_out1);
  Demultiplexer #(.enable("false")) demultiplexer_3 (
    .out0(demultiplexer_3_out0), .out1(demultiplexer_3_out1), .in(wait_for_RAM_q), .sel(multiplexer_1_out));
  Multiplexer #(.enable("false")) multiplexer_1 (
    .in0(ready_read), .in1(ready_write), .out(multiplexer_1_out), .sel(is_write));
  or or_6 (is_inst, demultiplexer_5_out0, get_data1);
  Demultiplexer #(.enable("false")) demultiplexer_4 (
    .out0(end_read), .out1(end_write), .in(demultiplexer_3_out1), .sel(is_write));
  and and_2 (tty_enable, PC_enable, is_tty);
  and and_3 (HI_LO_en, PC_enable, use_HI_LO);
  Priority_Encoder #(.select(2)) priority_encoder_1 (
    .in0(is_RF), .in1(MEM), .in2(is_PC), .in3(halt), .out(exe_select), .en_in(1'b1));  // open: gs, en_out
  D_Flip_Flop Fetch_instruction (
    .clk(clock), .D(is_inst), .Q(Fetch_instruction_q), .reset(reset));  // open: Qn, preset, en
  Demultiplexer #(.enable("false")) demultiplexer_5 (
    .out0(demultiplexer_5_out0), .out1(Inst__Memory_enable), .in(Fetch_instruction_q), .sel(ready_read));
  or or_7 (RF_enable, end_read, RF);
  Demultiplexer #(.select(2), .enable("false")) demultiplexer_6 (
    .out0(RF), .out1(mem_t), .out2(PC), .out3(demultiplexer_6_out3), .in(Save_inst_q), .sel(exe_select));
  D_Flip_Flop Save_inst (.clk(clock), .D(Inst__Memory_enable), .Q(Save_inst_q), .reset(reset));  // open: Qn, preset, en
  D_Flip_Flop Save (.clk(clock), .D(RF_enable), .Q(Save_q), .reset(reset));  // open: Qn, preset, en
  or or_8 (\end , END_q, demultiplexer_6_out3);
  or or_9 (PC_enable, Save_q, end_write, PC);
  D_Flip_Flop u_END (.clk(clock), .D(\end ), .Q(END_q), .reset(reset));  // open: Qn, preset, en

  // Other names for the same wires on the sheet: clk = clock; IM_en = Inst__Memory_enable; ready_r = ready_read;
  //   ready_w = ready_write; RF_en = RF_enable; tty_en = tty_enable; HI_LO = PC_enable; kbd_clear = PC_enable;
  //   next_inst = PC_enable; PC_en = PC_enable; tty_out = PC_enable

  // Notes on the sheet:
  //   Outputs
  //   Inputs
endmodule
