// Logisim project Memory Address.circ as structural Verilog: 1 circuit, main circuit Memory-Adress
module Memory_Adress (
  input  [31:0] ALU,
  input  [31:0] SP,
  input  [31:0] PC,
  input  sw,
  input  lw,
  input  pop,
  input  push,
  input  PC_Address,
  output [31:0] RAM_Dir
);

  wire [1:0] selector;
  wire [31:0] multiplexer_1_out, subtractor_1_out;

  Multiplexer #(.width(32), .enable("false")) multiplexer_1 (
    .in0(SP), .in1(subtractor_1_out), .out(multiplexer_1_out), .sel(push));
  Subtractor #(.width(32)) subtractor_1 (.a(SP), .b(32'h4), .out(subtractor_1_out));  // open: bin, bout
  or or_1 (selector[1], pop, PC_Address, push);
  or or_2 (selector[0], sw, PC_Address, lw);
  Multiplexer #(.select(2), .width(32), .enable("false")) multiplexer_2 (
    .in0(PC), .in1(ALU), .in2(multiplexer_1_out), .out(RAM_Dir), .sel(selector));  // open: in3

  // Notes on the sheet:
  //   Memory Adress
endmodule
