// Logisim project Program Counter.circ as structural Verilog: 1 circuit, main circuit Program-Counter
module Program_Counter (
  input  Clock,
  input  Enable,
  input  Reset,
  input  [31:0] Input,
  output [31:0] Output
);

  Register #(.width(32)) register_1 (.D(Input), .en(Enable), .Q(Output), .clk(Clock), .clr(Reset));

  // Notes on the sheet:
  //    COUNTER
  //   PROGRAM 
endmodule
