// Logisim project Register File Input.circ as structural Verilog: 1 circuit, main circuit Register-File-Input
module Register_File_Input (
  input  [2:0] Selector,
  input  clock,
  input  [31:0] RAM,
  input  KBD_available,
  input  [31:0] High,
  input  [31:0] ALU_Output,
  input  [6:0] Keyboard,
  input  [31:0] Low,
  output [31:0] RF_Input
);

  wire [31:0] KBD_in, random;

  Multiplexer #(.width(32), .enable("false")) multiplexer_1 (
    .in0({32{1'b1}}), .in1({{25{1'b0}}, Keyboard}), .out(KBD_in), .sel(KBD_available));
  Multiplexer #(.select(3), .width(32), .enable("false")) multiplexer_2 (
    .in0(ALU_Output), .in1(KBD_in), .in2(random), .in3(RAM), .in4(High), .in5(Low), .out(RF_Input),
    .sel(Selector));  // open: in6, in7
  Random #(.width(32)) Rnd (.clk(clock), .out(random));  // open: next, clr

  // Other names for the same wires on the sheet: ALU[31:0] = ALU_Output; clk = clock; KBD[6:0] = Keyboard;
  //   KBD_AVAIL = KBD_available

  // Notes on the sheet:
  //   Register File Input
endmodule
